# Fritzing sketch Fritzing (saved by Fritzing 0.9.5d)

parts:
  A1 = DORHEA ESP32 GPIO breakout board 30pin
  M1 = PH meter with sensor in breadboard [package=THT]
  A2 = tds-sensor-meter-v1.0_1
  U1 = Turbidity Sensor Probe [package=THT]
  DS1 = DS18B20 1-Wire Temperature Sensor Probe
  CPU1 = NodeMCU WROOM ESP 32  # not connected
  A3 = TS-300B interface

nets:
  N1: A1.Pin_27, A1.Pin_30, A1.Pin_32, A1.Pin_33, A1.Pin_34, A1.Pin_55, A1.Pin_56, A1.Pin_67, A1.Pin_81, A1.Pin_85, M1.pin1, M1.pin3, A2.pin1, A2.pin3, DS1.GND, DS1.DQ, A3.Pin_1, A3.Pin_2
  N2: A1.Pin_59, A1.Pin_60, M1.pin2, A3.Pin_4
  N3: A1.Pin_82, A2.pin2
  N4: A1.Pin_86, DS1.VDD
  N5: U1.pin1, A3.Pin_5
  N6: U1.pin2, A3.Pin_6
  N7: U1.VCC, A3.Pin_7

custom parts:
  DORHEA ESP32 GPIO breakout board 30pin: ESP32 shield 30P expansion board, supports two power supply : DC 6.5-16v and USB 5.V
  PH meter with sensor in breadboard: DFrobot PH meter (SKU SEN0161)
  : TDS Meter V1.0 Development Board Water Meter Filter Measuring Water Sensor Module.
  Turbidity Sensor Probe: Turbidity sensor probe to the DFRobot measure module.
  NodeMCU WROOM ESP 32: 30 pol Development Kit
  TS-300B interface: TS-300B interface.
